# Fritzing sketch SilentSleepSchematic (saved by Fritzing 1.0.7)
breadboards: 1

parts:
  A1 = Arduino UNO R4 WiFi
  TFT_Display = Adafruit 1.54inch 240x240 IPS TFT [part_number="Adafruit #3787"]
  DRV2605L_Haptic = Adafruit DRV2605L [part_number="Adafruit #2305"]
  MOTOR1 = Vibration Motor
  MIC = Adafruit MAX9814 Electret Microphone Amplifier [part_number="Adafruit #1713"]

nets:
  GND: A1.Pin_2, A1.Pin_9, A1.Pin_10, A1.Pin_25, TFT_Display.GND, DRV2605L_Haptic.GND, MIC.GND
  VIN: A1.Pin_8, A1.Pin_27, TFT_Display.VIN, DRV2605L_Haptic.VIN, MIC.VDD
  N1: A1.Pin_13, MIC.OUTPUT
  N2: A1.Pin_20, DRV2605L_Haptic.SDA
  N3: A1.Pin_21, DRV2605L_Haptic.SCL
  N4: A1.Pin_42, TFT_Display.TFTRST
  N5: A1.Pin_43, TFT_Display.TFTDC
  N6: A1.Pin_44, TFT_Display.TFTCS
  N7: A1.Pin_45, TFT_Display.MOSI
  N8: A1.Pin_47, TFT_Display.SCK
  N9: DRV2605L_Haptic.OUT+, MOTOR1.POS
  N10: DRV2605L_Haptic.OUT-, MOTOR1.NEG

custom parts:
  Arduino UNO R4 WiFi: The Arduino UNO R4 WiFi merges the RA4M1 microprocessor from Renesas with the ESP32-S3 from Espressif, creating an all-in-one tool for makers with enhanced processing power and a diverse array of new peripherals.
  Adafruit 1.54inch 240x240 IPS TFT: We've been looking for a display like this for a long time - it's only 1.5" diagonal but has a high density 220 ppi, 240x240 pixel display with full-angle viewing. It looks a lot like our 1.44" 128x128 display, but has 4x as many pixels and looks great at any angle. We've seen displays of this caliber used in smartwatches and small electronic devices but they've always been MIPI interface.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
  Adafruit DRV2605L: The DRV2605 from TI is a fancy little motor driver. Rather than controlling a stepper motor or DC motor, its designed specifically for controlling haptic motors - buzzers and vibration motors. Normally one would just turn those kinds of motors on and off, but this driver has the ability to have various effects when driving a vibe motor. For example, ramping the vibration level up and down,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
  Vibration Motor: An eccentric vibration motor!
  Adafruit MAX9814 Electret Microphone Amplifier: Add an ear to your project with this well-designed electret microphone amplifier with AGC. This fully assembled and tested board comes with a 20-20KHz electret microphone soldered on. For the amplification, we use the Maxim MAX9814, a specialty chip that is designed for amplifying electret microphones in situations where the loudness of the audio isn't predictable. This fancy microphone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
